// Logisim project Final_2.circ as structural Verilog: 2 circuits, main circuit main
module main (
  input  [13:0] in_1,
  input  in_2,
  input  [6:0] in_3,
  input  [13:0] in_4,
  input  [13:0] in_5,
  input  [6:0] in_6,
  input  in_7,
  input  [6:0] in_8,
  input  [13:0] in_9,
  input  [13:0] in_10,
  input  [6:0] in_11,
  input  in_12,
  input  [6:0] in_13,
  input  [13:0] in_14,
  input  [13:0] in_15,
  input  [6:0] in_16,
  input  in_17,
  input  [13:0] in_18,
  input  [6:0] in_19,
  input  [6:0] in_20,
  input  [13:0] in_21,
  input  in_22,
  input  [13:0] in_23,
  input  [6:0] in_24,
  input  [6:0] in_25,
  input  [13:0] in_26,
  input  [13:0] in_27,
  input  in_28,
  input  [6:0] in_29,
  input  [6:0] in_30,
  input  [13:0] in_31,
  input  [13:0] in_32,
  input  in_33,
  input  [6:0] in_34,
  input  [6:0] in_35,
  input  [13:0] in_36,
  input  [13:0] in_37,
  input  in_38,
  input  [6:0] in_39,
  input  [6:0] in_40,
  input  [6:0] in_41,
  input  [13:0] in_42,
  input  [13:0] in_43,
  input  in_44,
  input  [13:0] in_45,
  input  [6:0] in_46,
  input  [6:0] in_47,
  input  [13:0] in_48,
  input  [13:0] in_49,
  input  in_50,
  input  [6:0] in_51,
  input  [6:0] in_52,
  input  [13:0] in_53,
  input  in_54,
  input  [6:0] in_55,
  input  [13:0] in_56,
  input  [13:0] in_57,
  input  in_58,
  input  [6:0] in_59,
  input  [6:0] in_60,
  input  [13:0] in_61,
  input  [13:0] in_62,
  input  in_63,
  input  [6:0] in_64,
  input  [6:0] in_65,
  input  [13:0] in_66,
  input  [13:0] in_67,
  input  in_68,
  input  [6:0] in_69,
  input  [6:0] in_70,
  input  [13:0] in_71,
  input  [13:0] in_72,
  input  in_73,
  input  [6:0] in_74,
  input  [6:0] in_75,
  input  [13:0] in_76,
  input  [13:0] in_77,
  input  in_78,
  input  [6:0] in_79,
  input  [6:0] in_80,
  input  Fire,
  input  [13:0] in_82,
  input  [13:0] in_83,
  input  [6:0] in_84,
  input  in_85,
  input  [6:0] in_86,
  input  [13:0] in_87,
  input  [6:0] in_88,
  input  [13:0] in_89,
  input  [6:0] in_90,
  input  [13:0] in_91,
  input  [6:0] in_92,
  input  [13:0] in_93,
  input  [6:0] in_94,
  input  [13:0] in_95,
  input  [6:0] in_96,
  input  Box_Sensor
);

  wire and_1_out, and_2_out, and_4_out, and_10_out, and_11_out, and_12_out, and_13_out, and_24_out,
       and_25_out, and_26_out, and_27_out, and_28_out, and_29_out, and_30_out, and_32_out, and_33_out,
       and_34_out, and_35_out, and_36_out, and_37_out, and_38_out, and_39_out, and_44_out, and_45_out,
       and_46_out, and_47_out, and_48_out, and_49_out, and_50_out, and_51_out, and_52_out, and_53_out,
       and_54_out, and_55_out, and_56_out, and_57_out, and_58_out, and_59_out, and_64_out, and_65_out,
       and_66_out, and_67_out, and_68_out, and_69_out, and_70_out, and_71_out, and_72_out, and_73_out,
       and_74_out, and_75_out, and_76_out, and_77_out, and_78_out, and_79_out, and_84_out, b0, b1, b2, b3,
       b4, b5, b6, b7, b8, b9, bcd_to_7_segment_decoder_8_p1, button0, button1, button2, button3, button4,
       button5, button6, button7, button8, button9, clock_1_out, clock_2_out, clock_3_out, comparator_1_eq,
       comparator_1_gt, d_ff_1_q, d_ff_2_q, DF0_qn, DF1_qn, DF2_qn, digit0, Digit0Is0, Digit0Is10, digit1,
       Digit1Is0, Digit1Is10, digit2, Digit2Is0, Digit2Is10, digit3, Digit3Is0, Digit3Is10, dipswitch_1_p1,
       dipswitch_1_p2, dipswitch_1_p3, dipswitch_1_p4, dipswitch_2_p1, dipswitch_2_p2, dipswitch_2_p3,
       dipswitch_2_p4, dipswitch_3_p1, dipswitch_3_p2, dipswitch_3_p3, dipswitch_3_p4, dipswitch_4_p1,
       dipswitch_4_p2, dipswitch_4_p3, dipswitch_4_p4, Fire_t, InputNumber00, InputNumber01, InputNumber02,
       InputNumber03, InputNumber10, InputNumber11, InputNumber12, InputNumber13, InputNumber20,
       InputNumber21, InputNumber22, InputNumber23, InputNumber30, InputNumber31, InputNumber32,
       InputNumber33, isChangeable, isDissappeared, isFull, isInput, isOTP, isStart, isUnlocked,
       multiplexer_1_out, multiplexer_2_out, multiplexer_3_out, multiplexer_4_out, multiplexer_5_out,
       multiplexer_6_out, multiplexer_7_out, multiplexer_8_out, multiplexer_9_out, multiplexer_10_out,
       multiplexer_11_out, multiplexer_12_out, multiplexer_13_out, multiplexer_14_out, multiplexer_15_out,
       multiplexer_16_out, n7_segment_display_5_p1, Next_OTP_button, not_1_out, not_2_out, not_3_out,
       not_4_out, not_5_out, not_6_out, not_7_out, not_8_out, not_9_out, not_10_out, not_11_out, not_12_out,
       not_13_out, not_14_out, not_15_out, not_16_out, not_17_out, not_18_out, not_19_out, not_20_out,
       not_21_out, not_22_out, not_23_out, not_24_out, not_25_out, not_26_out, not_27_out, not_28_out,
       not_29_out, not_30_out, not_31_out, not_32_out, not_33_out, not_34_out, not_35_out, not_36_out,
       not_37_out, not_38_out, not_39_out, not_40_out, not_41_out, not_42_out, not_43_out, not_44_out,
       not_45_out, not_46_out, not_47_out, not_48_out, not_49_out, not_50_out, not_51_out, not_52_out,
       not_53_out, not_54_out, not_55_out, not_56_out, not_57_out, not_58_out, not_59_out, not_60_out,
       not_61_out, not_62_out, not_63_out, not_64_out, not_65_out, not_66_out, not_67_out, not_68_out,
       not_69_out, not_70_out, not_71_out, not_72_out, not_73_out, not_74_out, not_75_out, not_76_out,
       not_77_out, not_78_out, not_79_out, not_80_out, not_81_out, not_82_out, not_83_out, not_84_out,
       not_85_out, not_86_out, not_87_out, not_88_out, not_89_out, not_90_out, not_91_out, not_92_out,
       not_93_out, not_94_out, not_95_out, onesecondpulse_1_o, onesecondpulse_2_o, onesecondpulse_3_o,
       onesecondpulse_4_o, onesecondpulse_5_o, onesecondpulse_6_o, onesecondpulse_7_o, onesecondpulse_8_o,
       onesecondpulse_9_o, onesecondpulse_10_o, onesecondpulse_11_o, onesecondpulse_12_o,
       onesecondpulse_13_o, or_1_out, or_3_out, or_12_out, or_13_out, or_14_out, or_15_out, or_16_out,
       or_17_out, or_18_out, or_19_out, or_20_out, or_21_out, or_22_out, or_23_out, or_25_out, or_26_out,
       or_27_out, or_28_out, or_29_out, or_30_out, or_31_out, or_32_out, or_41_out, or_42_out, or_43_out,
       or_44_out, or_45_out, or_46_out, or_47_out, or_48_out, OTP_MODE_out, OTP_Number1_digit0,
       OTP_Number1_digit1, OTP_Number1_digit2, OTP_Number1_digit3, OTP_Number1Is0, OTP_Number2_digit0,
       OTP_Number2_digit1, OTP_Number2_digit2, OTP_Number2_digit3, OTP_Number2Is0, OTP_Number3_digit0,
       OTP_Number3_digit1, OTP_Number3_digit2, OTP_Number3_digit3, OTP_Number3Is0, OTP_Number4_digit0,
       OTP_Number4_digit1, OTP_Number4_digit2, OTP_Number4_digit3, OTP_Number4Is0, OTP_Number11,
       OTP_Number13, OTP_Number21, OTP_Number23, OTP_Number31, OTP_Number33, OTP_Number41, OTP_Number43,
       OTP_Reset, PowerOff, previous_OTPstate, Reset, Reset1, Reset2, Reset3, Reset_out, ResetKeypad,
       ResetThermometer_out, result0, result1, result2, result3, SGR_OTP_Number1_p4, SGR_OTP_Number2_p4,
       SGR_OTP_Number3_p4, SGR_OTP_Number4_p4, sharp, shift_register_1_p4, shift_register_3_p7,
       shift_register_3_p8, shift_register_3_p9, shift_register_3_p10, shift_register_5_p7,
       shift_register_5_p8, shift_register_5_p9, shift_register_5_p10, shift_register_7_p7,
       shift_register_7_p8, shift_register_7_p9, shift_register_7_p10, shift_register_9_p7,
       shift_register_9_p8, shift_register_9_p9, shift_register_9_p10, star, Start_Timer, t_ff_1_q, t_ff_2_q,
       t_ff_3_q, transmission_1_p1, transmission_2_p1, transmission_3_p1, transmission_4_p1,
       transmission_5_p1, updateSaved, xor_1_out, xor_2_out, xor_3_out, xor_4_out, xor_9_out, xor_10_out,
       xor_11_out, xor_12_out, xor_13_out, xor_14_out, xor_15_out, xor_16_out, xor_17_out, xor_18_out,
       xor_19_out, xor_20_out, xor_21_out, xor_22_out, xor_23_out, xor_24_out;
  wire [2:0] DF0_q, DFF0_q;
  wire [3:0] binary_to_bcd_converter_1_p2, binary_to_bcd_converter_1_p3, binary_to_bcd_converter_1_p4,
       divider_1_rem, divider_2_rem, divider_3_rem, divider_4_rem, InputNumber0, InputNumber1, InputNumber2,
       InputNumber3, SGR_OTP_Number1_p12, SGR_OTP_Number2_p12, SGR_OTP_Number3_p12, SGR_OTP_Number4_p12;
  wire [7:0] rom_1_data, rom_2_data;
  wire [8:0] counter_1_q;

  // Transmission_Gate transmission_1: pin names not known; wires that end beside it: transmission_1_p1, transmission_1_p1
  // Transmission_Gate transmission_2: pin names not known; wires that end beside it: transmission_2_p1, transmission_2_p1
  // Transmission_Gate transmission_3: pin names not known; wires that end beside it: transmission_3_p1, transmission_3_p1
  Button ResetThermometer (.out(ResetThermometer_out));
  and and_1 (and_1_out, clock_1_out, Fire);
  Clock clock_1 (.out(clock_1_out));
  T_Flip_Flop t_ff_1 (.T(1'b1), .clk(or_1_out), .Q(t_ff_1_q));  // open: Qn, reset, preset
  D_Flip_Flop DF0 (
    .D(DF0_qn), .clk(and_2_out), .Q(DF0_q[0]), .Qn(DF0_qn), .reset(ResetThermometer_out));  // open: preset
  and and_2 (and_2_out, and_1_out, not_3_out);
  or or_1 (or_1_out, Reset, Box_Sensor);
  not not_1 (not_1_out, isUnlocked);
  and and_3 (Reset1, isUnlocked, isDissappeared);
  not not_2 (not_2_out, Reset2);
  D_Flip_Flop d_ff_1 (.D(OTP_Reset), .clk(clock_2_out), .Q(d_ff_1_q));  // open: Qn, preset, reset
  Clock clock_2 (.out(clock_2_out));
  not not_3 (not_3_out, Fire_t);
  and and_4 (and_4_out, Box_Sensor, t_ff_1_q);
  and and_5 (Start_Timer, not_1_out, isDissappeared);
  or or_2 (Reset, Reset1, Reset2, Reset3);
  and and_6 (Reset3, Start_Timer, not_2_out, isUnlocked);
  Button u_Reset (.out(Reset_out));
  not not_4 (not_4_out, DF0_q[0]);
  D_Flip_Flop #(.trigger("high")) d_ff_2 (.D(not_5_out), .clk(1'b1), .Q(d_ff_2_q), .reset(Reset));  // open: Qn, preset
  not not_5 (not_5_out, and_4_out);
  D_Flip_Flop DFF0 (.D(not_9_out), .clk(d_ff_1_q), .Q(DFF0_q[0]), .preset(Reset_out));  // open: Qn, reset
  not not_6 (not_6_out, DFF0_q[0]);
  not not_7 (not_7_out, DFF0_q[1]);
  and and_7 (PowerOff, not_6_out, not_7_out, not_8_out);
  D_Flip_Flop DF1 (
    .D(DF1_qn), .clk(not_4_out), .Q(DF0_q[1]), .Qn(DF1_qn), .reset(ResetThermometer_out));  // open: preset
  not not_8 (not_8_out, DFF0_q[2]);
  D_Flip_Flop DFF1 (.D(not_13_out), .clk(DFF0_q[0]), .Q(DFF0_q[1]), .preset(Reset_out));  // open: Qn, reset
  not not_9 (not_9_out, DFF0_q[0]);
  ROM #(.addrWidth(3)) rom_1 (.addr(DFF0_q), .data(rom_1_data));
  D_Flip_Flop DF2 (
    .D(DF2_qn), .clk(not_10_out), .Q(DF0_q[2]), .Qn(DF2_qn), .reset(ResetThermometer_out));  // open: preset
  not not_10 (not_10_out, DF0_q[1]);
  not not_11 (not_11_out, DF0_q[0]);
  not not_12 (not_12_out, DF0_q[1]);
  ROM #(.addrWidth(3)) rom_2 (.addr(DF0_q), .data(rom_2_data));
  and and_8 (isDissappeared, d_ff_2_q, t_ff_1_q);
  not not_13 (not_13_out, DFF0_q[1]);
  and and_9 (Fire_t, not_11_out, not_12_out, DF0_q[2]);
  Clock clock_3 (.out(clock_3_out));
  D_Flip_Flop DFF2 (.D(not_14_out), .clk(DFF0_q[1]), .Q(DFF0_q[2]), .preset(Reset_out));  // open: Qn, reset
  Counter #(.max('h1ff), .width(9)) counter_1 (
    .clr(Reset), .up(1'b1), .count(Start_Timer), .clk(clock_3_out), .Q(counter_1_q));  // open: load, D, carry
  and and_10 (and_10_out, Box_Sensor, t_ff_2_q);
  not not_14 (not_14_out, DFF0_q[2]);
  // Buzzer NoBattery: pin names not known; wires that end beside it: in_45, PowerOff, in_41
  LedBar Thermometer (
    .led0(rom_2_data[7]), .led1(rom_2_data[6]), .led2(rom_2_data[5]), .led3(rom_2_data[4]),
    .led4(rom_2_data[3]), .led5(rom_2_data[2]), .led6(rom_2_data[1]), .led7(rom_2_data[0]));
  or or_3 (or_3_out, Reset2, and_10_out);
  LedBar Battery (
    .led0(rom_1_data[7]), .led1(rom_1_data[6]), .led2(rom_1_data[5]), .led3(rom_1_data[4]),
    .led4(rom_1_data[3]), .led5(rom_1_data[2]), .led6(rom_1_data[1]), .led7(rom_1_data[0]));
  LED led_1 (.in(PowerOff));
  T_Flip_Flop t_ff_2 (.T(1'b1), .clk(or_3_out), .Q(t_ff_2_q));  // open: Qn, reset, preset
  // Binary_to_BCD_converter binary_to_bcd_converter_1: pin names not known; wires that end beside it: counter_1_q, binary_to_bcd_converter_1_p2, binary_to_bcd_converter_1_p3, binary_to_bcd_converter_1_p4
  Hex_Digit_Display #(.decimalPoint("false")) hex_digit_display_1 (.value(binary_to_bcd_converter_1_p2));
  Hex_Digit_Display #(.decimalPoint("false")) hex_digit_display_2 (.value(binary_to_bcd_converter_1_p3));
  Comparator #(.mode("unsigned"), .width(9)) comparator_1 (
    .a(counter_1_q), .b(9'h3c), .gt(comparator_1_gt), .eq(comparator_1_eq));  // open: lt
  LED Warning (.in(t_ff_2_q));
  Hex_Digit_Display #(.decimalPoint("false")) hex_digit_display_3 (.value(binary_to_bcd_converter_1_p4));
  or or_4 (Reset2, comparator_1_gt, comparator_1_eq);
  T_Flip_Flop t_ff_3 (.T(1'b1), .clk(star), .Q(t_ff_3_q));  // open: Qn, reset, preset
  LED Can_change_password (.in(isChangeable));
  not not_15 (not_15_out, isChangeable);
  and and_11 (and_11_out, isFull, star);
  // Transmission_Gate transmission_4: pin names not known; wires that end beside it: transmission_4_p1, transmission_4_p1
  Button button_1 (.out(button1));
  Button button_2 (.out(button4));
  Button button_3 (.out(button7));
  Button button_4 (.out(star));
  or or_5 (isStart, sharp, star);
  and and_12 (and_12_out, result0, result1, result2, result3, not_15_out, isFull, star);
  not not_16 (not_16_out, and_12_out);
  and and_13 (and_13_out, t_ff_3_q, not_15_out, isFull, star);
  Button button_5 (.out(button2));
  Button button_6 (.out(button3));
  Button button_7 (.out(button5));
  Button button_8 (.out(button6));
  Button button_9 (.out(button8));
  Button button_10 (.out(button9));
  Button button_11 (.out(button0));
  Button button_12 (.out(sharp));
  Button u_ResetKeypad (.out(ResetKeypad));
  and and_14 (b0, t_ff_3_q, button0);
  and and_15 (b1, t_ff_3_q, button1);
  and and_16 (b2, t_ff_3_q, button2);
  and and_17 (b3, t_ff_3_q, button3);
  and and_18 (b4, t_ff_3_q, button4);
  and and_19 (b5, t_ff_3_q, button5);
  and and_20 (b6, t_ff_3_q, button6);
  and and_21 (b7, t_ff_3_q, button7);
  and and_22 (b8, t_ff_3_q, button8);
  and and_23 (b9, t_ff_3_q, button9);
  D_Flip_Flop d_ff_3 (.D(and_12_out), .clk(and_11_out), .Q(OTP_Reset), .reset(ResetKeypad));  // open: Qn, preset
  // Shift_Register #(.length(5)) shift_register_1: pin names not known; wires that end beside it: and_12_out, and_13_out, not_16_out, shift_register_1_p4
  LED Wrong_five_times (.in(shift_register_1_p4));
  or or_6 (isUnlocked, Fire_t, OTP_Reset);
  LED DoorOpen (.in(isUnlocked));
  and and_24 (and_24_out, sharp, t_ff_3_q);
  // _7_Segment_Display 7_segment_display_1: pin names not known; wires that end beside it: InputNumber3, InputNumber2
  // _7_Segment_Display 7_segment_display_2: pin names not known; wires that end beside it: InputNumber2, InputNumber1
  // BCD_to_7_Segment_decoder bcd_to_7_segment_decoder_1: pin names not known
  // BCD_to_7_Segment_decoder bcd_to_7_segment_decoder_2: pin names not known
  // Transmission_Gate transmission_5: pin names not known; wires that end beside it: transmission_5_p1, transmission_5_p1
  not not_17 (not_17_out, t_ff_3_q);
  or or_7 (digit0, b1, b3, b5, b7, b9);
  or or_8 (digit1, b0, b2, b3, b6, b7);
  or or_9 (digit2, b4, b5, b6, b7);
  or or_10 (digit3, b0, b8, b9);
  or or_11 (isInput, b0, b1, b2, b3, b4, b5, b6, b7, b8, b9);
  // _7_Segment_Display 7_segment_display_3: pin names not known; wires that end beside it: InputNumber1, InputNumber0
  // BCD_to_7_Segment_decoder bcd_to_7_segment_decoder_3: pin names not known
  T_Flip_Flop t_ff_4 (.T(1'b1), .clk(and_24_out), .Q(isChangeable), .reset(and_25_out));  // open: Qn, preset
  and and_25 (and_25_out, star, not_17_out);
  _7_Segment_Display u_7_segment_display_4 ();  // open: g, f, a, b, e, d, c, dp
  // BCD_to_7_Segment_decoder bcd_to_7_segment_decoder_4: pin names not known
  Button Next_OTP (.out(Next_OTP_button));
  not not_18 (not_18_out, isChangeable);
  and and_26 (and_26_out, not_18_out, and_24_out);
  and and_27 (and_27_out, isChangeable, digit0);
  and and_28 (and_28_out, isChangeable, digit1);
  and and_29 (and_29_out, isChangeable, digit2);
  and and_30 (and_30_out, isChangeable, digit3);
  or or_12 (or_12_out, ResetKeypad, isStart);
  // Shift_Register #(.length(4)) shift_register_2: pin names not known; wires that end beside it: or_12_out, isInput, digit0, InputNumber00
  or or_13 (or_13_out, ResetKeypad, and_26_out);
  // Shift_Register #(.length(4)) shift_register_3: pin names not known; wires that end beside it: or_13_out, updateSaved, and_27_out, InputNumber10, InputNumber20, InputNumber30, shift_register_3_p7, shift_register_3_p8, shift_register_3_p9, shift_register_3_p10
  or or_14 (or_14_out, ResetKeypad, isStart);
  // Shift_Register #(.length(4)) shift_register_4: pin names not known; wires that end beside it: or_14_out, isInput, digit1, InputNumber01
  or or_15 (or_15_out, ResetKeypad, and_26_out);
  // Shift_Register #(.length(4)) shift_register_5: pin names not known; wires that end beside it: or_15_out, updateSaved, and_28_out, InputNumber11, InputNumber21, InputNumber31, shift_register_5_p7, shift_register_5_p8, shift_register_5_p9, shift_register_5_p10
  or or_16 (or_16_out, ResetKeypad, isStart);
  // Shift_Register #(.length(4)) shift_register_6: pin names not known; wires that end beside it: or_16_out, isInput, digit2, InputNumber02
  or or_17 (or_17_out, ResetKeypad, and_26_out);
  // Shift_Register #(.length(4)) shift_register_7: pin names not known; wires that end beside it: or_17_out, updateSaved, and_29_out, InputNumber12, InputNumber22, InputNumber32, shift_register_7_p7, shift_register_7_p8, shift_register_7_p9, shift_register_7_p10
  or or_18 (or_18_out, ResetKeypad, isStart);
  // Shift_Register #(.length(4)) shift_register_8: pin names not known; wires that end beside it: or_18_out, isInput, digit3, InputNumber03
  or or_19 (or_19_out, ResetKeypad, and_26_out);
  // Shift_Register #(.length(4)) shift_register_9: pin names not known; wires that end beside it: or_19_out, updateSaved, and_30_out, InputNumber13, InputNumber23, InputNumber33, shift_register_9_p7, shift_register_9_p8, shift_register_9_p9, shift_register_9_p10
  xor xor_1 (xor_1_out, isOTP, previous_OTPstate);
  or or_20 (or_20_out, and_32_out, Next_OTP_button);
  xor xor_2 (xor_2_out, isOTP, previous_OTPstate);
  or or_21 (or_21_out, and_34_out, Next_OTP_button);
  xor xor_3 (xor_3_out, isOTP, previous_OTPstate);
  or or_22 (or_22_out, and_36_out, Next_OTP_button);
  xor xor_4 (xor_4_out, isOTP, previous_OTPstate);
  or or_23 (or_23_out, and_38_out, Next_OTP_button);
  and and_31 (updateSaved, isChangeable, isInput);
  and and_32 (and_32_out, isOTP, xor_1_out);
  and and_33 (and_33_out, Next_OTP_button, isOTP);
  // DipSwitch #(.number(4)) dipswitch_1: pin names not known; wires that end beside it: dipswitch_1_p1, dipswitch_1_p2, dipswitch_1_p3, dipswitch_1_p4
  and and_34 (and_34_out, isOTP, xor_2_out);
  and and_35 (and_35_out, Next_OTP_button, isOTP);
  // DipSwitch #(.number(4)) dipswitch_2: pin names not known; wires that end beside it: dipswitch_2_p1, dipswitch_2_p2, dipswitch_2_p3, dipswitch_2_p4
  and and_36 (and_36_out, isOTP, xor_3_out);
  and and_37 (and_37_out, Next_OTP_button, isOTP);
  // DipSwitch #(.number(4)) dipswitch_3: pin names not known; wires that end beside it: dipswitch_3_p1, dipswitch_3_p2, dipswitch_3_p3, dipswitch_3_p4
  and and_38 (and_38_out, isOTP, xor_4_out);
  and and_39 (and_39_out, Next_OTP_button, isOTP);
  // DipSwitch #(.number(4)) dipswitch_4: pin names not known; wires that end beside it: dipswitch_4_p1, dipswitch_4_p2, dipswitch_4_p3, dipswitch_4_p4
  // Shift_Register #(.length(4)) SGR_OTP_Number1: pin names not known; wires that end beside it: and_32_out, and_33_out, or_20_out, SGR_OTP_Number1_p4, dipswitch_1_p1, dipswitch_1_p2, dipswitch_1_p3, dipswitch_1_p4, SGR_OTP_Number1_p12[3], SGR_OTP_Number1_p12[2], SGR_OTP_Number1_p12[1], SGR_OTP_Number1_p12[0]
  // Shift_Register #(.length(4)) SGR_OTP_Number3: pin names not known; wires that end beside it: and_36_out, and_37_out, or_22_out, SGR_OTP_Number3_p4, dipswitch_3_p1, dipswitch_3_p2, dipswitch_3_p3, dipswitch_3_p4, SGR_OTP_Number3_p12[3], SGR_OTP_Number3_p12[2], SGR_OTP_Number3_p12[1], SGR_OTP_Number3_p12[0]
  // Shift_Register #(.length(4)) SGR_OTP_Number2: pin names not known; wires that end beside it: and_34_out, and_35_out, or_21_out, SGR_OTP_Number2_p4, dipswitch_2_p1, dipswitch_2_p2, dipswitch_2_p3, dipswitch_2_p4, SGR_OTP_Number2_p12[3], SGR_OTP_Number2_p12[2], SGR_OTP_Number2_p12[1], SGR_OTP_Number2_p12[0]
  // Shift_Register #(.length(4)) SGR_OTP_Number4: pin names not known; wires that end beside it: and_38_out, and_39_out, or_23_out, SGR_OTP_Number4_p4, dipswitch_4_p1, dipswitch_4_p2, dipswitch_4_p3, dipswitch_4_p4, SGR_OTP_Number4_p12[3], SGR_OTP_Number4_p12[2], SGR_OTP_Number4_p12[1], SGR_OTP_Number4_p12[0]
  xor xor_5 (SGR_OTP_Number1_p4, SGR_OTP_Number1_p12[3], SGR_OTP_Number1_p12[0]);
  xor xor_6 (SGR_OTP_Number2_p4, SGR_OTP_Number2_p12[3], SGR_OTP_Number2_p12[0]);
  xor xor_7 (SGR_OTP_Number3_p4, SGR_OTP_Number3_p12[3], SGR_OTP_Number3_p12[0]);
  xor xor_8 (SGR_OTP_Number4_p4, SGR_OTP_Number4_p12[3], SGR_OTP_Number4_p12[0]);
  or or_24 (isFull, InputNumber30, InputNumber31, InputNumber32, InputNumber33);
  Divider #(.width(4)) divider_1 (.a(SGR_OTP_Number1_p12), .b(4'b1010), .rem(divider_1_rem));  // open: out, upper
  Divider #(.width(4)) divider_2 (.a(SGR_OTP_Number2_p12), .b(4'b1010), .rem(divider_2_rem));  // open: out, upper
  Divider #(.width(4)) divider_3 (.a(SGR_OTP_Number3_p12), .b(4'b1010), .rem(divider_3_rem));  // open: out, upper
  Divider #(.width(4)) divider_4 (.a(SGR_OTP_Number4_p12), .b(4'b1010), .rem(divider_4_rem));  // open: out, upper
  Multiplexer multiplexer_1 (.in0(shift_register_7_p7), .in1(OTP_Number4_digit2), .out(multiplexer_1_out), .sel(isOTP));
  xor xor_9 (xor_9_out, InputNumber02, multiplexer_1_out);
  not not_19 (not_19_out, xor_9_out);
  not not_20 (not_20_out, Next_OTP_button);
  not not_21 (not_21_out, Next_OTP_button);
  not not_22 (not_22_out, Next_OTP_button);
  not not_23 (not_23_out, Next_OTP_button);
  Multiplexer multiplexer_2 (.in0(shift_register_3_p7), .in1(OTP_Number4_digit0), .out(multiplexer_2_out), .sel(isOTP));
  xor xor_10 (xor_10_out, InputNumber00, multiplexer_2_out);
  not not_24 (not_24_out, xor_10_out);
  Multiplexer multiplexer_3 (.in0(shift_register_5_p7), .in1(OTP_Number41), .out(multiplexer_3_out), .sel(isOTP));
  xor xor_11 (xor_11_out, InputNumber01, multiplexer_3_out);
  xor xor_12 (xor_12_out, InputNumber11, multiplexer_6_out);
  not not_25 (not_25_out, xor_11_out);
  not not_26 (not_26_out, xor_12_out);
  Multiplexer multiplexer_4 (.in0(shift_register_7_p8), .in1(OTP_Number3_digit2), .out(multiplexer_4_out), .sel(isOTP));
  xor xor_13 (xor_13_out, InputNumber12, multiplexer_4_out);
  not not_27 (not_27_out, xor_13_out);
  xor xor_14 (xor_14_out, InputNumber03, multiplexer_8_out);
  not not_28 (not_28_out, xor_14_out);
  // Shift_Register #(.length(4)) OTP_digit2: pin names not known; wires that end beside it: not_21_out, not_21_out, divider_1_rem[2], divider_2_rem[2], divider_3_rem[2], divider_4_rem[2], OTP_Number1_digit2, OTP_Number2_digit2, OTP_Number3_digit2, OTP_Number4_digit2
  // Shift_Register #(.length(4)) OTP_digit1: pin names not known; wires that end beside it: not_22_out, not_22_out, divider_1_rem[1], divider_2_rem[1], divider_3_rem[1], divider_4_rem[1], OTP_Number1_digit1, OTP_Number2_digit1, OTP_Number3_digit1, OTP_Number4_digit1
  // Shift_Register #(.length(4)) OTP_digit0: pin names not known; wires that end beside it: not_23_out, not_23_out, divider_1_rem[0], divider_2_rem[0], divider_3_rem[0], divider_4_rem[0], OTP_Number1_digit0, OTP_Number2_digit0, OTP_Number3_digit0, OTP_Number4_digit0
  Multiplexer multiplexer_5 (.in0(shift_register_3_p8), .in1(OTP_Number3_digit0), .out(multiplexer_5_out), .sel(isOTP));
  xor xor_15 (xor_15_out, InputNumber10, multiplexer_5_out);
  not not_29 (not_29_out, xor_15_out);
  Multiplexer multiplexer_6 (.in0(shift_register_5_p8), .in1(OTP_Number31), .out(multiplexer_6_out), .sel(isOTP));
  xor xor_16 (xor_16_out, InputNumber21, multiplexer_10_out);
  not not_30 (not_30_out, xor_16_out);
  Multiplexer multiplexer_7 (.in0(shift_register_7_p9), .in1(OTP_Number2_digit2), .out(multiplexer_7_out), .sel(isOTP));
  xor xor_17 (xor_17_out, InputNumber22, multiplexer_7_out);
  not not_31 (not_31_out, xor_17_out);
  Multiplexer multiplexer_8 (.in0(shift_register_9_p7), .in1(OTP_Number43), .out(multiplexer_8_out), .sel(isOTP));
  xor xor_18 (xor_18_out, InputNumber13, multiplexer_13_out);
  not not_32 (not_32_out, xor_18_out);
  // Shift_Register #(.length(4)) OTP_digit3: pin names not known; wires that end beside it: not_20_out, not_20_out, not_20_out, divider_1_rem[3], divider_2_rem[3], divider_3_rem[3], divider_4_rem[3], OTP_Number1_digit3, OTP_Number2_digit3, OTP_Number3_digit3, OTP_Number4_digit3
  Multiplexer multiplexer_9 (.in0(shift_register_3_p9), .in1(OTP_Number2_digit0), .out(multiplexer_9_out), .sel(isOTP));
  xor xor_19 (xor_19_out, InputNumber20, multiplexer_9_out);
  not not_33 (not_33_out, xor_19_out);
  Multiplexer multiplexer_10 (.in0(shift_register_5_p9), .in1(OTP_Number21), .out(multiplexer_10_out), .sel(isOTP));
  Multiplexer multiplexer_11 (.in0(shift_register_5_p10), .in1(OTP_Number11), .out(multiplexer_11_out), .sel(isOTP));
  xor xor_20 (xor_20_out, InputNumber31, multiplexer_11_out);
  not not_34 (not_34_out, xor_20_out);
  Multiplexer multiplexer_12 (
    .in0(shift_register_7_p10), .in1(OTP_Number1_digit2), .out(multiplexer_12_out), .sel(isOTP));
  xor xor_21 (xor_21_out, InputNumber32, multiplexer_12_out);
  not not_35 (not_35_out, xor_21_out);
  Multiplexer multiplexer_13 (.in0(shift_register_9_p8), .in1(OTP_Number33), .out(multiplexer_13_out), .sel(isOTP));
  Multiplexer multiplexer_14 (.in0(shift_register_9_p9), .in1(OTP_Number23), .out(multiplexer_14_out), .sel(isOTP));
  xor xor_22 (xor_22_out, InputNumber23, multiplexer_14_out);
  not not_36 (not_36_out, xor_22_out);
  Multiplexer multiplexer_15 (
    .in0(shift_register_3_p10), .in1(OTP_Number1_digit0), .out(multiplexer_15_out), .sel(isOTP));
  xor xor_23 (xor_23_out, InputNumber30, multiplexer_15_out);
  not not_37 (not_37_out, xor_23_out);
  and and_40 (result1, not_34_out, not_30_out, not_26_out, not_25_out);
  and and_41 (result2, not_35_out, not_31_out, not_27_out, not_19_out);
  Multiplexer multiplexer_16 (.in0(shift_register_9_p10), .in1(OTP_Number13), .out(multiplexer_16_out), .sel(isOTP));
  xor xor_24 (xor_24_out, InputNumber33, multiplexer_16_out);
  not not_38 (not_38_out, xor_24_out);
  and and_42 (result0, not_37_out, not_33_out, not_29_out, not_24_out);
  and and_43 (result3, not_38_out, not_36_out, not_32_out, not_28_out);
  or or_25 (or_25_out, Digit0Is0, Digit0Is10);
  or or_26 (or_26_out, Digit0Is0, Digit0Is10);
  or or_27 (or_27_out, Digit0Is0, Digit0Is10);
  or or_28 (or_28_out, Digit0Is0, Digit0Is10);
  or or_29 (or_29_out, Digit2Is0, Digit2Is10);
  or or_30 (or_30_out, Digit2Is0, Digit2Is10);
  or or_31 (or_31_out, Digit2Is0, Digit2Is10);
  or or_32 (or_32_out, Digit2Is0, Digit2Is10);
  not not_39 (not_39_out, or_25_out);
  not not_40 (not_40_out, or_26_out);
  not not_41 (not_41_out, or_27_out);
  not not_42 (not_42_out, or_28_out);
  and and_44 (and_44_out, Digit2Is0, 1'b0);
  not not_43 (not_43_out, or_29_out);
  and and_45 (and_45_out, not_43_out, InputNumber20);
  and and_46 (and_46_out, Digit2Is0, 1'b1);
  not not_44 (not_44_out, or_30_out);
  and and_47 (and_47_out, not_44_out, InputNumber21);
  and and_48 (and_48_out, Digit2Is0, 1'b0);
  not not_45 (not_45_out, or_31_out);
  and and_49 (and_49_out, not_45_out, InputNumber22);
  and and_50 (and_50_out, Digit2Is0, 1'b1);
  not not_46 (not_46_out, or_32_out);
  and and_51 (and_51_out, not_46_out, InputNumber23);
  not not_47 (not_47_out, InputNumber00);
  not not_48 (not_48_out, InputNumber01);
  not not_49 (not_49_out, InputNumber02);
  not not_50 (not_50_out, InputNumber03);
  not not_51 (not_51_out, InputNumber00);
  not not_52 (not_52_out, InputNumber02);
  and and_52 (and_52_out, Digit0Is0, 1'b0);
  and and_53 (and_53_out, not_39_out, InputNumber00);
  and and_54 (and_54_out, Digit0Is0, 1'b1);
  and and_55 (and_55_out, not_40_out, InputNumber01);
  and and_56 (and_56_out, Digit0Is0, 1'b0);
  and and_57 (and_57_out, not_41_out, InputNumber02);
  and and_58 (and_58_out, Digit0Is0, 1'b1);
  and and_59 (and_59_out, not_42_out, InputNumber03);
  not not_53 (not_53_out, InputNumber20);
  not not_54 (not_54_out, InputNumber21);
  not not_55 (not_55_out, InputNumber22);
  not not_56 (not_56_out, InputNumber23);
  not not_57 (not_57_out, InputNumber20);
  not not_58 (not_58_out, InputNumber22);
  or or_33 (InputNumber2[0], and_44_out, and_45_out);
  or or_34 (InputNumber2[1], and_46_out, and_47_out);
  or or_35 (InputNumber2[2], and_48_out, and_49_out);
  or or_36 (InputNumber2[3], and_50_out, and_51_out);
  or or_37 (InputNumber0[0], and_52_out, and_53_out);
  or or_38 (InputNumber0[1], and_54_out, and_55_out);
  or or_39 (InputNumber0[2], and_56_out, and_57_out);
  or or_40 (InputNumber0[3], and_58_out, and_59_out);
  and and_60 (Digit2Is0, not_53_out, not_54_out, not_55_out, not_56_out);
  and and_61 (Digit2Is10, not_57_out, InputNumber21, not_58_out, InputNumber23);
  // _7_Segment_Display 7_segment_display_5: pin names not known; wires that end beside it: n7_segment_display_5_p1, {OTP_Number1_digit3, OTP_Number1_digit2, OTP_Number1_digit1, OTP_Number1_digit0}, {OTP_Number2_digit3, OTP_Number2_digit2, OTP_Number2_digit1, OTP_Number2_digit0}
  // _7_Segment_Display 7_segment_display_6: pin names not known; wires that end beside it: {OTP_Number2_digit3, OTP_Number2_digit2, OTP_Number2_digit1, OTP_Number2_digit0}, {OTP_Number3_digit3, OTP_Number3_digit2, OTP_Number3_digit1, OTP_Number3_digit0}
  // BCD_to_7_Segment_decoder bcd_to_7_segment_decoder_5: pin names not known; wires that end beside it: n7_segment_display_5_p1
  // BCD_to_7_Segment_decoder bcd_to_7_segment_decoder_6: pin names not known
  and and_62 (Digit0Is0, not_47_out, not_48_out, not_49_out, not_50_out);
  and and_63 (Digit0Is10, not_51_out, InputNumber01, not_52_out, InputNumber03);
  Button OTP_MODE (.out(OTP_MODE_out));
  // _7_Segment_Display 7_segment_display_7: pin names not known; wires that end beside it: {OTP_Number3_digit3, OTP_Number3_digit2, OTP_Number3_digit1, OTP_Number3_digit0}, {OTP_Number4_digit3, OTP_Number4_digit2, OTP_Number4_digit1, OTP_Number4_digit0}
  _7_Segment_Display u_7_segment_display_8 ();  // open: g, f, a, b, e, d, c, dp
  // BCD_to_7_Segment_decoder bcd_to_7_segment_decoder_7: pin names not known
  // BCD_to_7_Segment_decoder bcd_to_7_segment_decoder_8: pin names not known; wires that end beside it: bcd_to_7_segment_decoder_8_p1, bcd_to_7_segment_decoder_8_p1
  T_Flip_Flop t_ff_5 (.T(1'b1), .clk(OTP_MODE_out), .Q(isOTP), .reset(OTP_Reset));  // open: Qn, preset
  or or_41 (or_41_out, Digit1Is0, Digit1Is10);
  or or_42 (or_42_out, Digit1Is0, Digit1Is10);
  or or_43 (or_43_out, Digit1Is0, Digit1Is10);
  or or_44 (or_44_out, Digit1Is0, Digit1Is10);
  or or_45 (or_45_out, Digit3Is0, Digit3Is10);
  or or_46 (or_46_out, Digit3Is0, Digit3Is10);
  or or_47 (or_47_out, Digit3Is0, Digit3Is10);
  or or_48 (or_48_out, Digit3Is0, Digit3Is10);
  D_Flip_Flop #(.trigger("falling")) d_ff_4 (
    .D(isOTP), .clk(OTP_MODE_out), .Q(previous_OTPstate));  // open: Qn, preset, reset
  not not_59 (not_59_out, or_41_out);
  not not_60 (not_60_out, or_42_out);
  not not_61 (not_61_out, or_43_out);
  not not_62 (not_62_out, or_44_out);
  and and_64 (and_64_out, Digit3Is0, 1'b0);
  not not_63 (not_63_out, or_45_out);
  and and_65 (and_65_out, not_63_out, InputNumber30);
  and and_66 (and_66_out, Digit3Is0, 1'b1);
  not not_64 (not_64_out, or_46_out);
  and and_67 (and_67_out, not_64_out, InputNumber31);
  and and_68 (and_68_out, Digit3Is0, 1'b0);
  not not_65 (not_65_out, or_47_out);
  and and_69 (and_69_out, not_65_out, InputNumber32);
  and and_70 (and_70_out, Digit3Is0, 1'b1);
  not not_66 (not_66_out, or_48_out);
  and and_71 (and_71_out, not_66_out, InputNumber33);
  not not_67 (not_67_out, InputNumber10);
  not not_68 (not_68_out, InputNumber11);
  not not_69 (not_69_out, InputNumber12);
  not not_70 (not_70_out, InputNumber13);
  not not_71 (not_71_out, InputNumber10);
  not not_72 (not_72_out, InputNumber12);
  and and_72 (and_72_out, Digit1Is0, 1'b0);
  or or_49 (InputNumber1[0], and_72_out, and_73_out);
  and and_73 (and_73_out, not_59_out, InputNumber10);
  and and_74 (and_74_out, Digit1Is0, 1'b1);
  or or_50 (InputNumber1[1], and_74_out, and_75_out);
  and and_75 (and_75_out, not_60_out, InputNumber11);
  and and_76 (and_76_out, Digit1Is0, 1'b0);
  or or_51 (InputNumber1[2], and_76_out, and_77_out);
  and and_77 (and_77_out, not_61_out, InputNumber12);
  and and_78 (and_78_out, Digit1Is0, 1'b1);
  or or_52 (InputNumber1[3], and_78_out, and_79_out);
  and and_79 (and_79_out, not_62_out, InputNumber13);
  not not_73 (not_73_out, InputNumber30);
  not not_74 (not_74_out, InputNumber31);
  not not_75 (not_75_out, InputNumber32);
  not not_76 (not_76_out, InputNumber33);
  not not_77 (not_77_out, InputNumber30);
  not not_78 (not_78_out, InputNumber32);
  or or_53 (InputNumber3[0], and_64_out, and_65_out);
  or or_54 (InputNumber3[1], and_66_out, and_67_out);
  or or_55 (InputNumber3[2], and_68_out, and_69_out);
  or or_56 (InputNumber3[3], and_70_out, and_71_out);
  and and_80 (Digit1Is0, not_67_out, not_68_out, not_69_out, not_70_out);
  and and_81 (Digit1Is10, not_71_out, InputNumber11, not_72_out, InputNumber13);
  and and_82 (Digit3Is0, not_73_out, not_74_out, not_75_out, not_76_out);
  and and_83 (Digit3Is10, not_77_out, InputNumber31, not_78_out, InputNumber33);
  and and_84 (and_84_out, star, not_79_out);
  not not_79 (not_79_out, OTP_Reset);
  OneSecondPulse onesecondpulse_1 (.I(button1), .O(onesecondpulse_1_o));
  OneSecondPulse onesecondpulse_2 (.I(button2), .O(onesecondpulse_2_o));
  OneSecondPulse onesecondpulse_3 (.I(button3), .O(onesecondpulse_3_o));
  OneSecondPulse onesecondpulse_4 (.I(button4), .O(onesecondpulse_4_o));
  OneSecondPulse onesecondpulse_5 (.I(button5), .O(onesecondpulse_5_o));
  OneSecondPulse onesecondpulse_6 (.I(button6), .O(onesecondpulse_6_o));
  OneSecondPulse onesecondpulse_7 (.I(button7), .O(onesecondpulse_7_o));
  OneSecondPulse onesecondpulse_8 (.I(button8), .O(onesecondpulse_8_o));
  OneSecondPulse onesecondpulse_9 (.I(button9), .O(onesecondpulse_9_o));
  OneSecondPulse onesecondpulse_10 (.I(button0), .O(onesecondpulse_10_o));
  OneSecondPulse onesecondpulse_11 (.I(OTP_Reset), .O(onesecondpulse_11_o));
  not not_80 (not_80_out, OTP_Number1_digit0);
  not not_81 (not_81_out, OTP_Number1_digit1);
  not not_82 (not_82_out, OTP_Number1_digit2);
  not not_83 (not_83_out, OTP_Number1_digit3);
  not not_84 (not_84_out, OTP_Number2_digit0);
  not not_85 (not_85_out, OTP_Number2_digit1);
  not not_86 (not_86_out, OTP_Number2_digit2);
  not not_87 (not_87_out, OTP_Number2_digit3);
  not not_88 (not_88_out, OTP_Number3_digit0);
  not not_89 (not_89_out, OTP_Number3_digit1);
  not not_90 (not_90_out, OTP_Number3_digit2);
  not not_91 (not_91_out, OTP_Number3_digit3);
  not not_92 (not_92_out, OTP_Number4_digit0);
  not not_93 (not_93_out, OTP_Number4_digit1);
  not not_94 (not_94_out, OTP_Number4_digit2);
  not not_95 (not_95_out, OTP_Number4_digit3);
  OneSecondPulse onesecondpulse_12 (.I(and_84_out), .O(onesecondpulse_12_o));
  OneSecondPulse onesecondpulse_13 (.I(sharp), .O(onesecondpulse_13_o));
  // Buzzer buzzer_1: pin names not known; wires that end beside it: in_4, onesecondpulse_1_o, in_6
  // Buzzer buzzer_2: pin names not known; wires that end beside it: in_9, onesecondpulse_2_o, in_11
  // Buzzer buzzer_3: pin names not known; wires that end beside it: in_14, onesecondpulse_3_o, in_16
  // Buzzer buzzer_4: pin names not known; wires that end beside it: in_18, onesecondpulse_4_o, in_20
  // Buzzer buzzer_5: pin names not known; wires that end beside it: in_23, onesecondpulse_5_o, in_25
  // Buzzer buzzer_6: pin names not known; wires that end beside it: in_27, onesecondpulse_6_o, in_30
  // Buzzer buzzer_7: pin names not known; wires that end beside it: in_32, onesecondpulse_7_o, in_35
  // Buzzer buzzer_8: pin names not known; wires that end beside it: in_37, onesecondpulse_8_o, in_40
  // Buzzer buzzer_9: pin names not known; wires that end beside it: in_42, onesecondpulse_9_o, in_46
  // Buzzer buzzer_10: pin names not known; wires that end beside it: in_48, onesecondpulse_10_o, in_51
  // Buzzer buzzer_11: pin names not known; wires that end beside it: in_56, onesecondpulse_11_o, in_59
  // Buzzer buzzer_12: pin names not known; wires that end beside it: in_61, onesecondpulse_11_o, in_64
  // Buzzer buzzer_13: pin names not known; wires that end beside it: in_66, onesecondpulse_11_o, in_69
  // Buzzer buzzer_14: pin names not known; wires that end beside it: in_71, onesecondpulse_11_o, in_74
  // Buzzer buzzer_15: pin names not known; wires that end beside it: in_76, onesecondpulse_12_o, in_79
  // Buzzer buzzer_16: pin names not known; wires that end beside it: in_82, onesecondpulse_12_o, in_84
  // Buzzer buzzer_17: pin names not known; wires that end beside it: in_87, onesecondpulse_12_o, in_88
  // Buzzer buzzer_18: pin names not known; wires that end beside it: in_89, onesecondpulse_13_o, in_90
  // Buzzer buzzer_19: pin names not known; wires that end beside it: in_91, onesecondpulse_13_o, in_92
  // Buzzer buzzer_20: pin names not known; wires that end beside it: in_93, onesecondpulse_13_o, in_94
  // Buzzer buzzer_21: pin names not known; wires that end beside it: in_95, onesecondpulse_13_o, in_96
  and and_85 (OTP_Number1Is0, not_80_out, not_81_out, not_82_out, not_83_out);
  or or_57 (OTP_Number11, OTP_Number1_digit1, OTP_Number1Is0);
  or or_58 (OTP_Number13, OTP_Number1_digit3, OTP_Number1Is0);
  and and_86 (OTP_Number2Is0, not_84_out, not_85_out, not_86_out, not_87_out);
  or or_59 (OTP_Number21, OTP_Number2_digit1, OTP_Number2Is0);
  or or_60 (OTP_Number23, OTP_Number2_digit3, OTP_Number2Is0);
  and and_87 (OTP_Number3Is0, not_88_out, not_89_out, not_90_out, not_91_out);
  or or_61 (OTP_Number31, OTP_Number3_digit1, OTP_Number3Is0);
  or or_62 (OTP_Number33, OTP_Number3_digit3, OTP_Number3Is0);
  and and_88 (OTP_Number4Is0, not_92_out, not_93_out, not_94_out, not_95_out);
  or or_63 (OTP_Number41, OTP_Number4_digit1, OTP_Number4Is0);
  or or_64 (OTP_Number43, OTP_Number4_digit3, OTP_Number4Is0);
  // Buzzer C: pin names not known; wires that end beside it: in_1, in_2, in_3
  // Buzzer C_s: pin names not known; wires that end beside it: in_5, in_7, in_8
  // Buzzer D: pin names not known; wires that end beside it: in_10, in_12, in_13
  // Buzzer D_s: pin names not known; wires that end beside it: in_15, in_17, in_19
  // Buzzer E: pin names not known; wires that end beside it: in_21, in_22, in_24
  // Buzzer F: pin names not known; wires that end beside it: in_26, in_28, in_29
  // Buzzer F_s: pin names not known; wires that end beside it: in_31, in_33, in_34
  // Buzzer G: pin names not known; wires that end beside it: in_36, in_38, in_39
  // Buzzer G_s: pin names not known; wires that end beside it: in_43, in_44, in_47
  // Buzzer A: pin names not known; wires that end beside it: in_49, in_50, in_52
  // Buzzer A_s: pin names not known; wires that end beside it: in_53, in_54, in_55
  // Buzzer B: pin names not known; wires that end beside it: in_57, in_58, in_60
  // Buzzer C1: pin names not known; wires that end beside it: in_62, in_63, in_65
  // Buzzer C1_s: pin names not known; wires that end beside it: in_67, in_68, in_70
  // Buzzer D1: pin names not known; wires that end beside it: in_72, in_73, in_75
  // Buzzer D1_s: pin names not known; wires that end beside it: in_77, in_78, in_80
  // Buzzer E1: pin names not known; wires that end beside it: in_83, in_85, in_86

  // Other names for the same wires on the sheet: starInput = star; OTP_Number10 = OTP_Number1_digit0;
  //   OTP_Number12 = OTP_Number1_digit2; OTP_Number20 = OTP_Number2_digit0; OTP_Number22 = OTP_Number2_digit2;
  //   OTP_Number30 = OTP_Number3_digit0; OTP_Number32 = OTP_Number3_digit2; OTP_Number40 = OTP_Number4_digit0;
  //   OTP_Number42 = OTP_Number4_digit2; PasswordCorrect = OTP_Reset; Time_Over = Reset2

  // Notes on the sheet:
  //   in_35: initial=0x8
  //   in_37: initial=0x416
  //   in_40: initial=0x8
  //   in_42: initial=0x497
  //   in_46: initial=0x8
  //   in_48: initial=0x527
  //   in_51: initial=0x8
  //   in_4: initial=0x20b
  //   in_6: initial=0x8
  //   in_9: initial=0x24b
  //   in_11: initial=0x8
  //   in_14: initial=0x293
  //   in_16: initial=0x8
  //   in_18: initial=0x2ba
  //   in_20: initial=0x8
  //   in_23: initial=0x310
  //   in_25: initial=0x8
  //   in_27: initial=0x370
  //   in_30: initial=0x8
  //   in_32: initial=0x3dc
  //   in_56: initial=0x20b
  //   in_59: initial=0x8
  //   in_61: initial=0x293
  //   in_64: initial=0x8
  //   in_66: initial=0x310
  //   in_69: initial=0x8
  //   in_71: initial=0x416
  //   in_74: initial=0x8
  //   in_76: initial=0x310
  //   in_79: initial=0x8
  //   in_82: initial=0x370
  //   in_84: initial=0x8
  //   in_87: initial=0x497
  //   in_88: initial=0x8
  //   in_89: initial=0x20b
  //   in_90: initial=0x8
  //   in_91: initial=0x293
  //   in_92: initial=0x8
  //   in_93: initial=0x310
  //   in_94: initial=0x8
  //   in_95: initial=0x3a4
  //   in_96: initial=0x8
  //   in_34: initial=0x8
  //   in_36: initial=0x310
  //   in_39: initial=0x8
  //   in_43: initial=0x33f
  //   in_47: initial=0x8
  //   in_49: initial=0x370
  //   in_52: initial=0x8
  //   in_53: initial=0x3a4
  //   in_55: initial=0x8
  //   in_57: initial=0x3dc
  //   in_60: initial=0x8
  //   in_62: initial=0x416
  //   in_65: initial=0x8
  //   in_67: initial=0x455
  //   in_70: initial=0x8
  //   in_72: initial=0x497
  //   in_75: initial=0x8
  //   in_77: initial=0x4dd
  //   in_80: initial=0x8
  //   in_83: initial=0x527
  //   in_86: initial=0x8
  //   in_1: initial=0x20b
  //   in_3: initial=0x8
  //   in_5: initial=0x22a
  //   in_8: initial=0x8
  //   in_10: initial=0x24b
  //   in_13: initial=0x8
  //   in_15: initial=0x26e
  //   in_19: initial=0x8
  //   in_21: initial=0x293
  //   in_24: initial=0x8
  //   in_26: initial=0x2ba
  //   in_29: initial=0x8
  //   in_31: initial=0x2e4
  //   배터리
  //   온도(불) 감지
  //   택배 감지
  //   contents of rom_1 (hex, n*v repeats v):
  //   0 80 c0 e0 f0 f8 fc fe
  //   contents of rom_2 (hex, n*v repeats v):
  //   0 80 c0 e0 f0 f8 fc fe
  //    1
  //    2
  //    4
  //    5
  //    7
  //    8
  //   별
  //    0
  //    3
  //    6
  //    9
  //   샵
  //   일시적인 비밀번호 OTP 관리
  //   도미솔도
  //   솔시레
  //   Auto-Tick Frequency 16Hz를 염두에 두고 만듦
endmodule

module OneSecondPulse (
  input  I,
  output O
);

  wire clock_1_out, comparator_1_eq;
  wire [2:0] counter_1_q;

  D_Flip_Flop d_ff_1 (.D(1'b1), .clk(I), .Q(O), .reset(comparator_1_eq));  // open: Qn, preset
  Clock clock_1 (.out(clock_1_out));
  Counter #(.max('h7), .width(3)) counter_1 (
    .clr(comparator_1_eq), .count(O), .clk(clock_1_out), .Q(counter_1_q));  // open: load, up, D, carry
  Comparator #(.width(3)) comparator_1 (.a(3'b111), .b(counter_1_q), .eq(comparator_1_eq));  // open: gt, lt
endmodule
